# Fritzing sketch buzzer (saved by Fritzing 0.9.2b)
breadboards: 1

parts:
  Raspberry_Pi1 = Raspberry Pi B+
  T1 = LM35 Temperature Sensor [package="TO92 [THT]"]
  J1 = Piezo Speaker
  R1 = Resistor [tolerance=±5% resistance=220 package=THT]

nets:
  N1: Raspberry_Pi1.GPIO17, R1.Pin_0
  N2: Raspberry_Pi1.GND, T1.+Vs
  N3: Raspberry_Pi1.5V, J1.pin2
  N4: T1.Vout, R1.Pin_1
  N5: T1.GND, J1.pin1
