# Fritzing sketch switch_onoff_led (saved by Fritzing 0.9.2b)
breadboards: 1

parts:
  Raspberry_Pi1 = Raspberry Pi B+
  S1 = Pushbutton [package="[THT]"]
  R1 = Resistor [tolerance=±5% resistance=220 package=THT]
  LED1 = LED - 5mm [color="Red (633nm)" package="5 mm [THT]"]
  R2 = Resistor [tolerance=±5% resistance=220 package=THT]

nets:
  N1: Raspberry_Pi1.GPIO24, LED1.anode
  N2: Raspberry_Pi1.GPIO23, S1.Pin_1, S1.Pin_2
  N3: Raspberry_Pi1.GND, R1.Pin_0, R2.Pin_0
  N4: S1.Pin_3, S1.Pin_4, R1.Pin_1
  N5: LED1.cathode, R2.Pin_1
